# Fritzing sketch Perfboard (saved by Fritzing 0.9.2b)
perfboards: 1

parts:
  Bauteil1 = Arduino Nano (Rev3.0) (ICSP)  # not connected
  LED9 = LED - 5mm [color="Blue (430nm)" package="5 mm [THT]"]
  LED10 = LED - 5mm [color="White (6500K)" package="5 mm [THT]"]
  LED11 = LED - 5mm [color="Red (633nm)" package="5 mm [THT]"]
  LED12 = LED - 5mm [color="Green (555nm)" package="5 mm [THT]"]
  LED13 = LED - 5mm [color="Red (633nm)" package="5 mm [THT]"]
  LED14 = LED - 5mm [color="Green (555nm)" package="5 mm [THT]"]
  LED15 = LED - 5mm [color="White (6500K)" package="5 mm [THT]"]
  LED16 = LED - 5mm [color="Blue (430nm)" package="5 mm [THT]"]
  R9 = Resistor [tolerance=±5% resistance=220 package=THT]
  R10 = Resistor [tolerance=±5% resistance=2.2k package=THT]
  R11 = Resistor [tolerance=±5% resistance=680 package=THT]
  R12 = Resistor [tolerance=±5% resistance=680 package=THT]
  R13 = Resistor [tolerance=±5% resistance=2.2k package=THT]
  R14 = Resistor [tolerance=±5% resistance=680 package=THT]
  R15 = Resistor [tolerance=±5% resistance=220 package=THT]
  R16 = Resistor [tolerance=±5% resistance=680 package=THT]
  U2 = 74HC595 [package="DIP16 [THT]"]
  U3 = 74HC595 [package="DIP16 [THT]"]  # not connected
  R26 = Resistor [tolerance=±5% resistance=10k package=THT]  # not connected
  R27 = Resistor [tolerance=±5% resistance=10k package=THT]  # not connected
  R28 = Resistor [tolerance=±5% resistance=10k package=THT]  # not connected
  R29 = Resistor [tolerance=±5% resistance=10k package=THT]  # not connected
  R30 = Resistor [tolerance=±5% resistance=10k package=THT]  # not connected
  R31 = Resistor [tolerance=±5% resistance=10k package=THT]  # not connected
  R32 = Resistor [tolerance=±5% resistance=10k package=THT]  # not connected
  R33 = Resistor [tolerance=±5% resistance=10k package=THT]  # not connected
  R34 = Resistor [tolerance=±5% resistance=1k package=THT]
  R35 = Resistor [tolerance=±5% resistance=1k package=THT]  # not connected
  R36 = Resistor [tolerance=±5% resistance=1k package=THT]
  R37 = Resistor [tolerance=±5% resistance=1k package=THT]
  R38 = Resistor [tolerance=±5% resistance=1k package=THT]  # not connected
  R39 = Resistor [tolerance=±5% resistance=1k package=THT]
  R40 = Resistor [tolerance=±5% resistance=1k package=THT]
  R41 = Resistor [tolerance=±5% resistance=1k package=THT]

nets:
  N1: LED9.cathode, R12.Pin_1
  N2: LED10.cathode, R10.Pin_1
  N3: LED11.cathode, R11.Pin_1
  N4: LED12.cathode, R9.Pin_1
  N5: LED13.cathode, R14.Pin_1
  N6: LED14.cathode, R15.Pin_1
  N7: LED15.cathode, R13.Pin_1
  N8: LED16.cathode, R16.Pin_1
  N9: LED16.anode, U2.Q5
  N10: R34.Pin_0, R37.Pin_0, R41.Pin_0
  N11: R36.Pin_0, R39.Pin_0, R40.Pin_0

notes:
  Masse
  10K Vorw. 165
  5V
  1K Vorw. Buttons
  -
  +
  LED 1-8
  Button 1-8
  74HC165
