# Fritzing sketch Piano (saved by Fritzing 0.9.2b)
circuit board: 12.2908cm x 7.41512cm
breadboards: 2

parts:
  Arduino_Nano = Arduino Nano (Rev3.0) (ICSP)
  U2 = 74HC595 [package="DIP16 [THT]"]
  S1 = Pushbutton [package="[SMD]"]
  S2 = Pushbutton [package="[SMD]"]
  S3 = Pushbutton [package="[SMD]"]
  S5 = Pushbutton [package="[SMD]"]
  S6 = Pushbutton [package="[SMD]"]
  S7 = Pushbutton [package="[SMD]"]
  S8 = Pushbutton [package="[SMD]"]
  R1 = Resistor [tolerance=±5% resistance=680 package=THT]
  R2 = Resistor [tolerance=±5% resistance=220 package=THT]
  R3 = Resistor [tolerance=±5% resistance=680 package=THT]
  R4 = Resistor [tolerance=±5% resistance=2.2k package=THT]
  R5 = Resistor [tolerance=±5% resistance=680 package=THT]
  R6 = Resistor [tolerance=±5% resistance=220 package=THT]
  R7 = Resistor [tolerance=±5% resistance=680 package=THT]
  R8 = Resistor [tolerance=±5% resistance=2.2k package=THT]
  LED1 = LED - 5mm [color="Red (633nm)" package="5 mm [THT]"]
  LED2 = LED - 5mm [color="Green (555nm)" package="5 mm [THT]"]
  LED3 = LED - 5mm [color="Blue (430nm)" package="5 mm [THT]"]
  LED4 = LED - 5mm [color="White (6500K)" package="5 mm [THT]"]
  LED5 = LED - 5mm [color="Red (633nm)" package="5 mm [THT]"]
  LED6 = LED - 5mm [color="Green (555nm)" package="5 mm [THT]"]
  LED7 = LED - 5mm [color="Blue (430nm)" package="5 mm [THT]"]
  LED8 = LED - 5mm [color="White (6500K)" package="5 mm [THT]"]
  SP1 = SPEAKER [package=pcb_mount_speaker]
  S4 = Pushbutton [package="[SMD]"]
  74HC165 = 74HC595 [package="DIP16 [THT]"]
  R9 = Resistor [tolerance=±5% resistance=10k package=THT]
  R11 = Resistor [tolerance=±5% resistance=10k package=THT]
  R12 = Resistor [tolerance=±5% resistance=10k package=THT]
  R13 = Resistor [tolerance=±5% resistance=1k package=THT]
  R14 = Resistor [tolerance=±5% resistance=1k package=THT]
  R15 = Resistor [tolerance=±5% resistance=1k package=THT]
  R16 = Resistor [tolerance=±5% resistance=1k package=THT]
  R17 = Resistor [tolerance=±5% resistance=1k package=THT]
  R18 = Resistor [tolerance=±5% resistance=1k package=THT]
  R19 = Resistor [tolerance=±5% resistance=1k package=THT]
  R20 = Resistor [tolerance=±5% resistance=1k package=THT]
  R21 = Resistor [tolerance=±5% resistance=10k package=THT]
  R22 = Resistor [tolerance=±5% resistance=10k package=THT]
  R23 = Resistor [tolerance=±5% resistance=10k package=THT]
  R24 = Resistor [tolerance=±5% resistance=10k package=THT]
  R25 = Resistor [tolerance=±5% resistance=10k package=THT]

nets:
  GND: Arduino_Nano.GND, U2.GND, U2.OE, R1.Pin_0, R2.Pin_0, R3.Pin_0, R4.Pin_0, R5.Pin_0, R6.Pin_0, R7.Pin_0, R8.Pin_0, SP1.+, 74HC165.Q7, 74HC165.GND, 74HC165.MR, R9.Pin_1, R11.Pin_1, R12.Pin_1, R21.Pin_0, R22.Pin_0, R23.Pin_0, R24.Pin_0, R25.Pin_1
  N1: Arduino_Nano.D5, SP1.-
  N2: Arduino_Nano.D6, 74HC165.Q1
  N3: Arduino_Nano.D7, 74HC165.Q0
  N4: Arduino_Nano.D8, 74HC165.Q7'
  N5: Arduino_Nano.D9, 74HC165.Q2
  N6: Arduino_Nano.D10, U2.ST_CP
  N7: Arduino_Nano.D11/MOSI, U2.DS
  N8: Arduino_Nano.D12/MISO, U2.SH_CP
  VCC: Arduino_Nano.5V, U2.MR, U2.VCC, 74HC165.VCC, R13.Pin_1, R14.Pin_1, R15.Pin_1, R16.Pin_1, R17.Pin_1, R18.Pin_1, R19.Pin_1, R20.Pin_1
  N9: U2.Q1, LED2.anode
  N10: U2.Q2, LED3.anode
  N11: U2.Q3, LED4.anode
  N12: U2.Q4, LED5.anode
  N13: U2.Q5, LED6.anode
  N14: U2.Q6, LED7.anode
  N15: U2.Q7, LED8.anode
  N16: U2.Q0, LED1.anode
  N17: S1.Pin_1, S1.Pin_2, R20.Pin_0
  N18: S1.Pin_3, S1.Pin_4, 74HC165.SH_CP, R9.Pin_0
  N19: S2.Pin_1, S2.Pin_2, R19.Pin_0
  N20: S2.Pin_3, S2.Pin_4, 74HC165.ST_CP, R25.Pin_0
  N21: S3.Pin_1, S3.Pin_2, R18.Pin_0
  N22: S3.Pin_3, S3.Pin_4, 74HC165.OE, R11.Pin_0
  N23: S5.Pin_1, S5.Pin_2, R16.Pin_0
  N24: S5.Pin_3, S5.Pin_4, 74HC165.Q3, R24.Pin_1
  N25: S6.Pin_1, S6.Pin_2, R15.Pin_0
  N26: S6.Pin_3, S6.Pin_4, 74HC165.Q4, R23.Pin_1
  N27: S7.Pin_1, S7.Pin_2, R13.Pin_0
  N28: S7.Pin_3, S7.Pin_4, 74HC165.Q6, R21.Pin_1
  N29: S8.Pin_1, S8.Pin_2, R14.Pin_0
  N30: S8.Pin_3, S8.Pin_4, 74HC165.Q5, R22.Pin_1
  N31: R1.Pin_1, LED1.cathode
  N32: R2.Pin_1, LED2.cathode
  N33: R3.Pin_1, LED3.cathode
  N34: R4.Pin_1, LED4.cathode
  N35: R5.Pin_1, LED5.cathode
  N36: R6.Pin_1, LED6.cathode
  N37: R7.Pin_1, LED7.cathode
  N38: R8.Pin_1, LED8.cathode
  N39: S4.Pin_1, S4.Pin_2, R17.Pin_0
  N40: S4.Pin_3, S4.Pin_4, 74HC165.DS, R12.Pin_0

notes:
  This 74* IC is a 74HC165 (multiple inputs)
